# Fritzing sketch RTE (saved by Fritzing 0.9.6b)

parts:
  Part1 = Adafruit ADS1115 16Bit I2C ADC [part_number="Adafruit #1085"]
  M1 = MAX30102
  Mod2 = AD8232 HeartRate Monitor [part_number=SEN-12650]
  A1 = Raspberry Pi 4B

nets:
  N1: Part1.AIN0, Mod2.OUTPUT
  N2: Part1.SDA, M1.SDA, A1.GPIO2
  N3: Part1.SCL, M1.SCL, A1.GPIO3
  GND: Part1.GND, M1.GND, Mod2.GND, A1.GND
  VDD: Part1.VDD, M1.VIN, Mod2.3.3v, A1.3V3
  N4: Mod2.LO-, A1.GPIO23
  N5: Mod2.LO+, A1.GPIO24

custom parts:
  Adafruit ADS1115 16Bit I2C ADC: For microcontrollers without an analog-to-digital converter or when you want a higher-precision ADC, the ADS1115 provides 16-bit precision at 860 samples/second over I2C. The chip can be configured as 4 single-ended input channels, or two differential channels. As a nice bonus, it even includes a programmable gain amplifier, up to x16, to help boost up smaller single/differential signals to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
  MAX30102: Oximeter module using the MAX30102 chip. You may wish to read (and check your module) this post on power problems with these modules: https://reedpaper.wordpress.com/2018/08/22/pulse-oximeter-max30100-max30102-how-to-fix-wrong-board/ . As usual, if you want the mounting holes in pcb, you need to drag a hole over the pad in silkscreen to actually drill the hole (by default they are not drilled)
  AD8232 HeartRate Monitor: Sparkfun single lead heart rate monitor - Ad8232.
